// Logisim project ALU.circ as structural Verilog: 3 circuits, main circuit main
module main (
  input  [3:0] A,
  input  cin,
  input  [3:0] B,
  input  _0,
  input  _1,
  input  [1:0] s1_s0,
  output [3:0] \output ,
  output cout
);

  wire adder_1_cout, adder_2_cout, adder_3_cout, multiplexer_1_out, multiplexer_2_out, multiplexer_3_out,
       multiplexer_4_out, not_1_out, not_2_out, not_3_out, not_4_out;

  not not_1 (not_1_out, B[0]);
  not not_2 (not_2_out, B[1]);
  not not_3 (not_3_out, B[2]);
  not not_4 (not_4_out, B[3]);
  Multiplexer #(.select(2), .enable("false")) multiplexer_1 (
    .in0(B[0]), .in1(not_1_out), .in2(_0), .in3(_1), .out(multiplexer_1_out), .sel(s1_s0));
  Multiplexer #(.select(2), .enable("false")) multiplexer_2 (
    .in0(B[1]), .in1(not_2_out), .in2(_0), .in3(_1), .out(multiplexer_2_out), .sel(s1_s0));
  Multiplexer #(.select(2), .enable("false")) multiplexer_3 (
    .in0(B[2]), .in1(not_3_out), .in2(_0), .in3(_1), .out(multiplexer_3_out), .sel(s1_s0));
  Multiplexer #(.select(2), .enable("false")) multiplexer_4 (
    .in0(B[3]), .in1(not_4_out), .in2(_0), .in3(_1), .out(multiplexer_4_out), .sel(s1_s0));
  Adder #(.width(1)) adder_1 (.a(A[0]), .b(multiplexer_1_out), .out(\output [0]), .cin(cin), .cout(adder_1_cout));
  Adder #(.width(1)) adder_2 (
    .a(A[1]), .b(multiplexer_2_out), .out(\output [1]), .cin(adder_1_cout), .cout(adder_2_cout));
  Adder #(.width(1)) adder_3 (
    .a(A[2]), .b(multiplexer_3_out), .out(\output [2]), .cin(adder_2_cout), .cout(adder_3_cout));
  Adder #(.width(1)) adder_4 (.a(A[3]), .b(multiplexer_4_out), .out(\output [3]), .cin(adder_3_cout), .cout(cout));
endmodule

module ALU (
  input  [3:0] A,
  input  [3:0] B,
  input  [1:0] s1_s0,
  output [3:0] E
);

  wire [3:0] and_1_out, not_1_out, or_1_out, xor_1_out;

  assign and_1_out = A & B;  // AND_Gate and_1, 4 bits wide
  assign or_1_out = A | B;  // OR_Gate or_1, 4 bits wide
  assign xor_1_out = A ^ B;  // XOR_Gate xor_1, 4 bits wide
  assign not_1_out = ~A;  // NOT_Gate not_1, 4 bits wide
  Multiplexer #(.select(2), .width(4), .enable("false")) multiplexer_1 (
    .in0(and_1_out), .in1(or_1_out), .in2(xor_1_out), .in3(not_1_out), .out(E), .sel(s1_s0));
endmodule

module combined (
  input  [3:0] B,
  input  [3:0] A,
  input  cin,
  input  in_4,
  input  in_5,
  input  [1:0] s1_s0,
  input  [1:0] s3_s2,
  input  [1:0] _1_shift,
  input  [1:0] _1_shift_2,
  output [3:0] final_output
);

  wire [3:0] alu_1_e, main_1_output, shifter_1_out, shifter_2_out;

  Shifter #(.width(4), .shift("lr")) shifter_1 (.in(A), .\dist (_1_shift), .out(shifter_1_out));
  Shifter #(.width(4)) shifter_2 (.in(A), .\dist (_1_shift_2), .out(shifter_2_out));
  main main_1 (.A(A), .cin(cin), .B(B), ._0(in_4), ._1(in_5), .s1_s0(s1_s0), .\output (main_1_output));  // open: cout
  ALU alu_1 (.A(A), .B(B), .s1_s0(s1_s0), .E(alu_1_e));
  Multiplexer #(.select(2), .width(4), .enable("false")) multiplexer_1 (
    .in0(main_1_output), .in1(alu_1_e), .in2(shifter_1_out), .in3(shifter_2_out), .out(final_output),
    .sel(s3_s2));
endmodule
