// Logisim project ControlCircuit.circ as structural Verilog: 5 circuits, main circuit main
module main (
  input  in_1,
  input  [6:0] in_2,
  input  Z,
  input  S,
  input  U
);

  wire clock_1_out, i_p_logic_1_l, maincircuit_1_i;
  wire [1:0] i_p_logic_1_s0, m_ad_1_br, m_ad_1_cd;
  wire [2:0] m_ad_1_f1, m_ad_1_f2, m_ad_1_f3;
  wire [5:2] maincircuit_1_map;
  wire [6:0] adder_1_out, CAR_q, m_ad_1_ad, multiplexer_1_out, SBR_q;
  wire [19:0] rom_1_data;

  Clock clock_1 (.out(clock_1_out));
  Multiplexer #(.select(2), .width(7)) multiplexer_1 (
    .in1(m_ad_1_ad), .in2(SBR_q), .in3({1'b0, maincircuit_1_map, 2'b00}), .out(multiplexer_1_out),
    .sel(i_p_logic_1_s0));  // open: in0, en
  I_P_Logic i_p_logic_1 (
    .U(U), .I(maincircuit_1_i), .S(S), .BR(m_ad_1_br), .Z(Z), .CD(m_ad_1_cd), .S0(i_p_logic_1_s0[0]),
    .S1(i_p_logic_1_s0[1]), .L(i_p_logic_1_l));
  Register #(.width(7), .trigger("falling")) CAR (
    .D(multiplexer_1_out), .Q(CAR_q), .clk(clock_1_out));  // open: en, clr
  MainCircuit maincircuit_1 (
    .F1(m_ad_1_f1), .F2(m_ad_1_f2), .F3(m_ad_1_f3), .MAP(maincircuit_1_map), .I(maincircuit_1_i));
  Adder #(.width(7)) adder_1 (.a(in_2), .b(CAR_q), .out(adder_1_out), .cin(in_1));  // open: cout
  Register #(.width(7), .trigger("falling")) SBR (
    .D(adder_1_out), .en(i_p_logic_1_l), .Q(SBR_q), .clk(clock_1_out));  // open: clr
  M_AD m_ad_1 (
    .DR(rom_1_data), .AD(m_ad_1_ad), .BR(m_ad_1_br), .CD(m_ad_1_cd), .F1(m_ad_1_f1), .F2(m_ad_1_f2),
    .F3(m_ad_1_f3));
  ROM #(.addrWidth(7), .dataWidth(20)) rom_1 (.addr(CAR_q), .data(rom_1_data));  // open: sel

  // Notes on the sheet:
  //   contents of rom_1 (hex, n*v repeats v):
  //   12*0 53465 51*0 c0041 12842 a0180
endmodule

module M_AD (
  input  [19:0] DR,
  output [6:0] AD,
  output [1:0] BR,
  output [1:0] CD,
  output [2:0] F1,
  output [2:0] F2,
  output [2:0] F3
);


  assign AD = DR[6:0];
  assign BR = DR[8:7];
  assign CD = DR[10:9];
  assign F1 = DR[13:11];
  assign F2 = DR[16:14];
  assign F3 = DR[19:17];
endmodule

module I_P_Logic (
  input  U,
  input  I,
  input  S,
  input  [1:0] BR,
  input  Z,
  input  [1:0] CD,
  output S0,
  output S1,
  output L
);

  wire and_1_out, and_2_out, multiplexer_1_out, not_1_out;

  Multiplexer #(.select(2)) multiplexer_1 (
    .in0(U), .in1(I), .in2(S), .in3(Z), .out(multiplexer_1_out), .sel(CD));  // open: en
  not not_1 (not_1_out, BR[1]);
  and and_1 (and_1_out, BR[0], BR[1]);
  and and_2 (and_2_out, multiplexer_1_out, not_1_out);
  and and_3 (L, BR[0], not_1_out, multiplexer_1_out);
  or or_1 (S0, and_1_out, and_2_out);

  assign S1 = BR[1];
endmodule

module ALS (
  input  ADD,
  input  [15:0] A,
  input  in_3,
  input  [15:0] B,
  input  TF,
  output [15:0] OUT
);

  wire [15:0] adder_1_out, and_1_out, and_2_out, bit_extender_1_out, bit_extender_2_out;

  Adder #(.width(16)) adder_1 (.a(A), .b(B), .out(adder_1_out), .cin(in_3));  // open: cout
  assign bit_extender_1_out = {{15{TF}}, TF};  // Bit_Extender bit_extender_1
  assign bit_extender_2_out = {{15{ADD}}, ADD};  // Bit_Extender bit_extender_2
  assign and_1_out = bit_extender_2_out & adder_1_out;  // AND_Gate and_1, 16 bits wide
  assign and_2_out = A & bit_extender_1_out;  // AND_Gate and_2, 16 bits wide
  assign OUT = and_1_out | and_2_out;  // OR_Gate or_1, 16 bits wide
endmodule

module MainCircuit (
  input  [2:0] F1,
  input  [2:0] F2,
  input  [2:0] F3,
  output [3:0] MAP,
  output I
);

  wire _3, _4, _6, ADD, clock_1_out, decoder_1_out5, decoder_1_out6, decoder_2_out7, DRL, DRTAC, or_1_out,
       or_2_out;
  wire [10:0] AR_q, bit_extender_2_out, DR_q, multiplexer_1_out, PC_q;
  wire [15:0] AC_q, als_1_out, bit_extender_1_out, multiplexer_2_out, rom_1_data;

  Clock clock_1 (.out(clock_1_out));
  Decoder #(.select(3)) decoder_1 (
    .out1(ADD), .out4(DRTAC), .out5(decoder_1_out5), .out6(decoder_1_out6), .sel(F1));  // open: out0, out2, out3, out7, en
  Multiplexer #(.width(11)) multiplexer_1 (
    .in0(PC_q), .in1(bit_extender_2_out), .out(multiplexer_1_out), .sel(decoder_1_out6));  // open: en
  or or_1 (or_1_out, decoder_1_out5, decoder_1_out6);
  Register #(.width(11), .trigger("falling")) AR (
    .D(multiplexer_1_out), .en(or_1_out), .Q(AR_q), .clk(clock_1_out));  // open: clr
  Counter #(.width(11), .max('h7ff), .trigger("falling")) PC (
    .load(_6), .D(AR_q), .Q(PC_q), .clk(clock_1_out));  // open: count, carry, clr
  Decoder #(.select(3)) decoder_2 (
    .out3(_3), .out4(_4), .out7(decoder_2_out7), .sel(F2));  // open: out0, out1, out2, out5, out6, en
  assign bit_extender_1_out = {{5{1'b0}}, PC_q};  // Bit_Extender bit_extender_1
  Multiplexer #(.width(16)) multiplexer_2 (
    .in0(rom_1_data), .in1(bit_extender_1_out), .out(multiplexer_2_out), .sel(decoder_2_out7));  // open: en
  Bit_Extender #(.in_width(16), .out_width(11)) bit_extender_2 (.in({I, MAP, DR_q}), .out(bit_extender_2_out));
  or or_2 (or_2_out, ADD, DRTAC);
  ROM #(.addrWidth(11), .dataWidth(16)) rom_1 (.addr(AR_q), .data(rom_1_data));  // open: sel
  Register #(.width(16), .trigger("falling")) DR (
    .D(multiplexer_2_out), .en(DRL), .Q({I, MAP, DR_q}), .clk(clock_1_out));  // open: clr
  Register #(.width(16), .trigger("falling")) AC (
    .D(als_1_out), .en(or_2_out), .Q(AC_q), .clk(clock_1_out));  // open: clr
  or or_3 (DRL, _4, decoder_2_out7);
  ALS als_1 (.ADD(ADD), .A({I, MAP, DR_q}), .B(AC_q), .TF(DRTAC), .OUT(als_1_out));  // open: in_3
  Decoder #(.select(3)) decoder_3 (.out6(_6), .sel(F3));  // open: out0, out1, out2, out3, out4, out5, out7, en

  // Notes on the sheet:
  //   contents of rom_1 (hex, n*v repeats v):
  //   2222 3333
endmodule
