// Logisim project MYFETCH.circ as structural Verilog: 4 circuits, main circuit main
module main (
  input  in_1
);

  wire and_1_out, and_2_out, clock_1_out, decoder_1_out0, decoder_1_out1, decoder_1_out2, not_1_out, or_3_out;
  wire [1:0] counter_1_q;
  wire [2:0] or_2_out;
  wire [11:0] adder_1_out, AR_q, n1to12_1_o, PC_q;
  wire [15:0] IR_q, multiplexer_1_out, n12to16_1_out_3, n12to16_2_out_3, ram_1_data;

  Counter #(.width(2), .max('h3)) counter_1 (.Q(counter_1_q), .clk(clock_1_out));  // open: load, D, count, carry, clr
  Clock clock_1 (.out(clock_1_out));
  _1to12 u_1to12_1 (.I(decoder_1_out1), .in_2(in_1), .O(n1to12_1_o));
  Decoder #(.select(2), .enable("false")) decoder_1 (
    .out0(decoder_1_out0), .out1(decoder_1_out1), .out2(decoder_1_out2), .sel(counter_1_q));  // open: out3
  or or_1 (or_2_out[1], decoder_1_out0, decoder_1_out1);
  or or_2 (or_2_out[0], decoder_1_out1, decoder_1_out2);
  or or_3 (or_3_out, decoder_1_out0, decoder_1_out2);
  Adder #(.width(12)) adder_1 (.a(PC_q), .b(n1to12_1_o), .out(adder_1_out));  // open: cin, cout
  or or_4 (or_2_out[2], decoder_1_out2, decoder_1_out1);
  not not_1 (not_1_out, in_1);
  RAM #(.addrWidth(12), .dataWidth(16), .bus("separate")) ram_1 (
    .addr(AR_q), .data(ram_1_data), .clk(clock_1_out), .ld(and_1_out));  // open: din, str, sel, clr
  Register #(.width(12)) AR (.D(PC_q), .en(or_3_out), .Q(AR_q), .clk(clock_1_out));  // open: clr
  Register #(.width(12)) PC (.D(adder_1_out), .en(not_1_out), .Q(PC_q), .clk(clock_1_out));  // open: clr
  Register #(.width(16)) IR (.D(multiplexer_1_out), .en(decoder_1_out1), .Q(IR_q), .clk(clock_1_out));  // open: clr
  and and_1 (and_1_out, or_2_out[1], and_2_out);
  _12to16 u_12to16_1 (.i(AR_q), .in_2(in_1), .out_3(n12to16_1_out_3));
  _12to16 u_12to16_2 (.i(PC_q), .in_2(in_1), .out_3(n12to16_2_out_3));
  and and_2 (and_2_out, or_2_out[2], or_2_out[0]);
  Multiplexer #(.select(3), .width(16), .enable("false")) multiplexer_1 (
    .in1(n12to16_1_out_3), .in2(n12to16_2_out_3), .in5(IR_q), .in7(ram_1_data), .out(multiplexer_1_out),
    .sel(or_2_out));  // open: in0, in3, in4, in6
endmodule

module _1to16 (
  input  I,
  output [15:0] O
);


  assign O = {16{I}};
endmodule

module _1to12 (
  input  I,
  input  in_2,
  output [11:0] O
);


  assign O = {{11{in_2}}, I};
endmodule

module _12to16 (
  input  [11:0] i,
  input  in_2,
  output [15:0] out_3
);


  assign out_3 = {{4{in_2}}, i};
endmodule
