// Logisim project PRAC1_B.circ as structural Verilog: 1 circuit, main circuit main
module main (
  input  [1:0] in_1,
  input  in_2,
  input  in_3
);

  wire adder_1_cout, adder_1_out, and_1_out, clock_1_out, comparator_1_eq, d_ff_1_q, or_1_out,
       shift_register_1_out, shift_register_2_out, xor_1_out;
  wire [1:0] counter_1_q;

  Shift_Register #(.length(4)) shift_register_1 (
    .in(adder_1_out), .clk(clock_1_out), .out(shift_register_1_out));  // open: shift, load, clr, d0, q0, d1, q1, d2, q2, d3, q3
  Shift_Register #(.length(4)) shift_register_2 (
    .in(shift_register_2_out), .clk(clock_1_out), .out(shift_register_2_out));  // open: shift, load, clr, d0, q0, d1, q1, d2, q2, d3, q3
  Clock clock_1 (.out(clock_1_out));
  xor xor_1 (xor_1_out, shift_register_2_out, in_3);
  Adder #(.width(1)) adder_1 (
    .a(shift_register_1_out), .b(xor_1_out), .out(adder_1_out), .cin(or_1_out), .cout(adder_1_cout));
  or or_1 (or_1_out, and_1_out, d_ff_1_q);
  D_Flip_Flop d_ff_1 (.clk(clock_1_out), .D(adder_1_cout), .Q(d_ff_1_q), .en(in_2));  // open: Qn, preset, reset
  Counter #(.width(2), .max('h3)) counter_1 (.Q(counter_1_q), .clk(clock_1_out));  // open: load, D, count, carry, clr
  Comparator #(.width(2)) comparator_1 (.a(in_1), .b(counter_1_q), .eq(comparator_1_eq));  // open: gt, lt
  and and_1 (and_1_out, comparator_1_eq, in_3);
endmodule
