// Logisim project PRAC1_C.circ as structural Verilog: 1 circuit, main circuit main
module main (
  input  [3:0] in_1,
  input  [3:0] in_2,
  input  in_3,
  input  [3:0] in_4,
  input  [3:0] in_5,
  input  in_6,
  output out_7,
  output [3:0] out_8,
  output [3:0] out_9
);

  wire [3:0] adder_1_out, adder_2_out;
  wire [3:1] adder_1_cout;
  wire [3:3] not_2_out;

  Adder #(.width(4)) adder_1 (.a(in_1), .b(in_2), .out(adder_1_out), .cout(adder_1_cout[1]));  // open: cin
  Adder #(.width(4)) adder_2 (.a(in_4), .b(in_5), .out(adder_2_out), .cin(adder_1_cout[1]), .cout(out_7));
  not not_1 (adder_1_cout[3], adder_1_cout[1]);
  not not_2 (not_2_out[3], out_7);
  Adder #(.width(4)) adder_3 (
    .a(adder_1_out), .b({{2{adder_1_cout[3]}}, adder_1_cout[1], in_3}), .out(out_9));  // open: cin, cout
  Adder #(.width(4)) adder_4 (.a(adder_2_out), .b({{2{not_2_out[3]}}, out_7, in_6}), .out(out_8));  // open: cin, cout
endmodule
