// Logisim project bus_system_parellal.circ as structural Verilog: 1 circuit, main circuit main
module main (
  input  [1:0] in_1,
  input  [1:0] in_2
);

  wire clock_1_out, decoder_1_out0, decoder_1_out1, decoder_1_out2, decoder_1_out3;
  wire [3:0] multiplexer_1_out, register_1_q, register_2_q, register_3_q, register_4_q;

  Decoder #(.select(2), .enable("false")) decoder_1 (
    .out0(decoder_1_out0), .out1(decoder_1_out1), .out2(decoder_1_out2), .out3(decoder_1_out3), .sel(in_1));
  Clock clock_1 (.out(clock_1_out));
  Register #(.width(4)) register_1 (
    .D(multiplexer_1_out), .en(decoder_1_out0), .Q(register_1_q), .clk(clock_1_out));  // open: clr
  Register #(.width(4)) register_2 (
    .D(multiplexer_1_out), .en(decoder_1_out1), .Q(register_2_q), .clk(clock_1_out));  // open: clr
  Register #(.width(4)) register_3 (
    .D(multiplexer_1_out), .en(decoder_1_out2), .Q(register_3_q), .clk(clock_1_out));  // open: clr
  Register #(.width(4)) register_4 (
    .D(multiplexer_1_out), .en(decoder_1_out3), .Q(register_4_q), .clk(clock_1_out));  // open: clr
  Multiplexer #(.select(2), .width(4), .enable("false")) multiplexer_1 (
    .in0(register_1_q), .in1(register_2_q), .in2(register_3_q), .in3(register_4_q), .out(multiplexer_1_out),
    .sel(in_2));
endmodule
