// Logisim project serial_bus_sys_UPDATED.circ as structural Verilog: 2 circuits, main circuit main
module main (
  input  [3:0] R1,
  input  [3:0] R2,
  input  CLOCK,
  input  [3:0] R3,
  input  [1:0] input_register_selection,
  input  [1:0] output_register_selection,
  input  [3:0] R4
);

  wire and_1_out, controlled_buffer_1_out, counter_1_carry, decoder_1_out0, decoder_1_out1, decoder_1_out2,
       decoder_1_out3, decoder_2_out0, decoder_2_out1, decoder_2_out2, decoder_2_out3, not_1_out, or_1_out,
       or_2_out, or_3_out, or_4_out, REGISTER_1_out, REGISTER_2_out, REGISTER_3_out, REGISTER_4_out;

  Counter #(.width(3), .max('h4), .ongoal("stay")) counter_1 (
    .carry(counter_1_carry), .clk(CLOCK));  // open: load, D, count, Q, clr
  not not_1 (not_1_out, counter_1_carry);
  Decoder #(.select(2), .enable("false")) decoder_1 (
    .out0(decoder_1_out0), .out1(decoder_1_out1), .out2(decoder_1_out2), .out3(decoder_1_out3),
    .sel(input_register_selection));
  and and_1 (and_1_out, not_1_out, CLOCK);
  or or_1 (or_1_out, decoder_2_out0, decoder_1_out0);
  or or_2 (or_2_out, decoder_2_out1, decoder_1_out1);
  or or_3 (or_3_out, decoder_2_out2, decoder_1_out2);
  or or_4 (or_4_out, decoder_2_out3, decoder_1_out3);
  Shift_Register #(.length(4)) REGISTER_1 (
    .shift(or_1_out), .in(controlled_buffer_1_out), .clk(and_1_out), .out(REGISTER_1_out), .d0(R1[3]),
    .d1(R1[2]), .d2(R1[1]), .d3(R1[0]));  // open: load, clr, q0, q1, q2, q3
  Shift_Register #(.length(4)) REGISTER_2 (
    .shift(or_2_out), .in(controlled_buffer_1_out), .clk(and_1_out), .out(REGISTER_2_out), .d0(R2[3]),
    .d1(R2[2]), .d2(R2[1]), .d3(R2[0]));  // open: load, clr, q0, q1, q2, q3
  Shift_Register #(.length(4)) REGISTER_3 (
    .shift(or_3_out), .in(controlled_buffer_1_out), .clk(and_1_out), .out(REGISTER_3_out), .d0(R3[3]),
    .d1(R3[2]), .d2(R3[1]), .d3(R3[0]));  // open: load, clr, q0, q1, q2, q3
  Shift_Register #(.length(4)) REGISTER_4 (
    .shift(or_4_out), .in(controlled_buffer_1_out), .clk(and_1_out), .out(REGISTER_4_out), .d0(R4[3]),
    .d1(R4[2]), .d2(R4[1]), .d3(R4[0]));  // open: load, clr, q0, q1, q2, q3
  assign controlled_buffer_1_out = decoder_1_out0 ? REGISTER_1_out : 1'bz;  // Controlled_Buffer controlled_buffer_1
  assign controlled_buffer_1_out = decoder_1_out1 ? REGISTER_2_out : 1'bz;  // Controlled_Buffer controlled_buffer_2
  assign controlled_buffer_1_out = decoder_1_out2 ? REGISTER_3_out : 1'bz;  // Controlled_Buffer controlled_buffer_3
  assign controlled_buffer_1_out = decoder_1_out3 ? REGISTER_4_out : 1'bz;  // Controlled_Buffer controlled_buffer_4
  Decoder #(.select(2), .enable("false")) decoder_2 (
    .out0(decoder_2_out0), .out1(decoder_2_out1), .out2(decoder_2_out2), .out3(decoder_2_out3),
    .sel(output_register_selection));
endmodule

module tcx (
  input  [3:0] R1,
  input  [3:0] R2,
  input  [3:0] R3,
  input  [3:0] R4,
  input  [1:0] OUTPUT_REGISTER,
  input  [1:0] INPUT_REGISTER
);

  wire clock_1_out;

  Clock clock_1 (.out(clock_1_out));
  main main_1 (
    .R1(R1), .R2(R2), .CLOCK(clock_1_out), .R3(R3), .output_register_selection(OUTPUT_REGISTER), .R4(R4),
    .input_register_selection(INPUT_REGISTER));
endmodule
