// Logisim project UpdateFetchFINAL.circ as structural Verilog: 9 circuits, main circuit main
module main (
  input  FGI,
  output out_2
);

  wire and_2_out, and_3_out, and_6_out, and_7_out, and_8_out, and_9_out, and_10_out, b9_1_o, clock_1_out,
       decoder_1_out0, decoder_1_out1, decoder_1_out3, decoder_1_out4, decoder_1_out5, decoder_1_out6,
       decoder_1_out7, decoder_2_out0, decoder_2_out1, decoder_2_out2, decoder_2_out3, decoder_2_out4,
       decoder_2_out5, n12to1_1_o, or_1_out, or_2_out, or_5_out, or_8_out;
  wire [2:0] ir_12_14_1_out, or_7_out;
  wire [3:0] counter_2_q;
  wire [11:0] and_1_out, AR_q, counter_1_q, n1to12_1_out_2, n16to12_1_out_2, n16to12_2_out_2;
  wire [15:0] AC_q, adder_1_out, and_4_out, and_5_out, DR_q, IR_q, multiplexer_1_out, n1_16_1__16,
       n1_16_2__16, n12to16_1_out_3, n12to16_2_out_3, or_3_out, rom_1_data;

  B9 b9_1 (.i(IR_q), .o(b9_1_o));
  assign and_1_out = n1to12_1_out_2 & AR_q;  // AND_Gate and_1, 12 bits wide
  or or_1 (or_1_out, and_2_out, decoder_2_out1);
  and and_2 (and_2_out, decoder_1_out7, FGI, out_2, b9_1_o, decoder_2_out3);
  _1to12 u_1to12_1 (.i(and_3_out), .out_2(n1to12_1_out_2));
  _12to1 u_12to1_1 (.i(and_1_out), .o(n12to1_1_o));
  and and_3 (and_3_out, decoder_2_out3, out_2);
  Decoder #(.select(3)) decoder_1 (
    .out0(decoder_1_out0), .out1(decoder_1_out1), .out3(decoder_1_out3), .out4(decoder_1_out4),
    .out5(decoder_1_out5), .out6(decoder_1_out6), .out7(decoder_1_out7), .sel(ir_12_14_1_out));  // open: out2, en
  IR_15 ir_15_1 (.in_1(IR_q), .out_2(out_2));
  IR_12_14 ir_12_14_1 (.IR(IR_q), .out(ir_12_14_1_out));
  _1_16 u_1_16_1 (._1(decoder_1_out0), ._16(n1_16_1__16));
  _1_16 u_1_16_2 (._1(decoder_1_out1), ._16(n1_16_2__16));
  _16To12 u_16to12_1 (.in_1(multiplexer_1_out), .out_2(n16to12_1_out_2));
  Adder #(.width(16)) adder_1 (.a(DR_q), .b(AC_q), .out(adder_1_out));  // open: cin, cout
  _16To12 u_16to12_2 (.in_1(multiplexer_1_out), .out_2(n16to12_2_out_2));
  or or_2 (or_2_out, decoder_2_out3, decoder_2_out2, decoder_2_out0);
  assign and_4_out = DR_q & n1_16_1__16 & AC_q;  // AND_Gate and_4, 16 bits wide
  assign or_3_out = and_4_out | and_5_out;  // OR_Gate or_3, 16 bits wide
  assign and_5_out = adder_1_out & n1_16_2__16;  // AND_Gate and_5, 16 bits wide
  ROM #(.addrWidth(12), .dataWidth(16)) rom_1 (.addr(AR_q), .data(rom_1_data), .sel(or_5_out));
  Register #(.width(12), .trigger("falling")) AR (
    .D(n16to12_2_out_2), .en(or_2_out), .Q(AR_q), .clk(clock_1_out));  // open: clr
  Counter #(.width(12), .max('hfff)) counter_1 (
    .load(and_6_out), .D(n16to12_1_out_2), .count(or_1_out), .Q(counter_1_q), .clk(clock_1_out));  // open: carry, clr
  Register #(.width(16), .trigger("falling")) IR (
    .D(multiplexer_1_out), .en(decoder_2_out1), .Q(IR_q), .clk(clock_1_out));  // open: clr
  Register #(.width(16)) DR (.D(multiplexer_1_out), .en(or_8_out), .Q(DR_q), .clk(clock_1_out));  // open: clr
  Register #(.width(16)) AC (.D(or_3_out), .en(decoder_2_out5), .Q(AC_q), .clk(clock_1_out));  // open: clr
  _12To16 u_12to16_1 (._12(AR_q), .out_3(n12to16_1_out_3));  // open: in_2
  _12To16 u_12to16_2 (._12(counter_1_q), .out_3(n12to16_2_out_3));  // open: in_2
  and and_6 (and_6_out, decoder_2_out4, decoder_1_out4);
  and and_7 (and_7_out, decoder_1_out4, decoder_2_out5);
  Multiplexer #(.select(3), .width(16)) multiplexer_1 (
    .in1(n12to16_1_out_3), .in2(n12to16_2_out_3), .in3(DR_q), .in4(AC_q), .in5(IR_q), .in7(rom_1_data),
    .out(multiplexer_1_out), .sel(or_7_out));  // open: in0, in6, en
  or or_4 (or_7_out[1], and_10_out, decoder_2_out0, and_9_out, decoder_2_out1, and_8_out);
  or or_5 (or_5_out, n12to1_1_o, and_10_out, and_8_out, decoder_2_out1);
  or or_6 (or_7_out[2], and_10_out, decoder_2_out1, and_9_out, decoder_2_out2, and_8_out);
  or or_7 (or_7_out[0], and_10_out, decoder_2_out2, decoder_2_out1, and_6_out, and_8_out);
  Clock clock_1 (.out(clock_1_out));
  or or_8 (or_8_out, decoder_2_out5, decoder_2_out4);
  and and_8 (and_8_out, decoder_2_out4, decoder_1_out1);
  and and_9 (and_9_out, decoder_1_out0, decoder_2_out5);
  and and_10 (and_10_out, decoder_1_out0, decoder_2_out4);
  Decoder #(.select(4)) decoder_2 (
    .out0(decoder_2_out0), .out1(decoder_2_out1), .out2(decoder_2_out2), .out3(decoder_2_out3),
    .out4(decoder_2_out4), .out5(decoder_2_out5), .sel(counter_2_q));  // open: out6, out7, out8, out9, out10, out11, out12, out13, out14, out15, en
  Counter #(.width(4), .max('h5), .trigger("falling")) counter_2 (
    .Q(counter_2_q), .clk(clock_1_out), .clr(and_7_out));  // open: load, D, count, carry

  // Notes on the sheet:
  //   contents of rom_1 (hex, n*v repeats v):
  //   1001 3 4007 3007 3007 ffd4 1007 f200 1369*0 8561
  //   PC
endmodule

module _12To16 (
  input  [11:0] _12,
  input  [3:0] in_2,
  output [15:0] out_3
);


  assign out_3 = {in_2, _12};
endmodule

module _16To12 (
  input  [15:0] in_1,
  output [11:0] out_2
);


  assign out_2 = in_1[11:0];
endmodule

module IR_12_14 (
  input  [15:0] IR,
  output [2:0] out
);


  assign out = IR[14:12];
endmodule

module IR_15 (
  input  [15:0] in_1,
  output out_2
);


  assign out_2 = in_1[15];
endmodule

module _1_16 (
  input  _1,
  output [15:0] _16
);

  assign _16 = {{15{_1}}, _1};  // Bit_Extender bit_extender_1
endmodule

module _1to12 (
  input  i,
  output [11:0] out_2
);


  assign out_2 = {12{i}};
endmodule

module _12to1 (
  input  [11:0] i,
  output o
);

  Bit_Extender #(.in_width(12), .out_width(1)) bit_extender_1 (.in(i), .out(o));
endmodule

module B9 (
  input  [15:0] i,
  output o
);


  assign o = i[9];
endmodule
