// Logisim project booth.circ as structural Verilog: 2 circuits, main circuit main
module main (
  input  [7:0] in_1
);

  wire AC_out, and_1_out, clock_1_out, counter_1_q, not_1_out, not_3_out, or_1_out, Q_n_1_out, Q_out, Q_q7,
       xor_1_out;
  wire [7:0] AC_q7, adder_1_out, adder_2_out, and_2_out, and_3_out, B_q7, n1to8_1_output, n1to8_2_output,
       n1to8_3_output, not_2_out, or_2_out;

  and and_1 (and_1_out, not_1_out, xor_1_out);
  Clock clock_1 (.out(clock_1_out));
  not not_1 (not_1_out, counter_1_q);
  Shift_Register AC (
    .shift(or_1_out), .in(AC_q7[7]), .clk(clock_1_out), .out(AC_out), .load(and_1_out), .d0(adder_2_out[7]),
    .q0(AC_q7[7]), .d1(adder_2_out[6]), .q1(AC_q7[6]), .d2(adder_2_out[5]), .q2(AC_q7[5]),
    .d3(adder_2_out[4]), .q3(AC_q7[4]), .d4(adder_2_out[3]), .q4(AC_q7[3]), .d5(adder_2_out[2]),
    .q5(AC_q7[2]), .d6(adder_2_out[1]), .q6(AC_q7[1]), .d7(adder_2_out[0]), .q7(AC_q7[0]));  // open: clr
  Shift_Register B (
    .q0(B_q7[7]), .q1(B_q7[6]), .q2(B_q7[5]), .q3(B_q7[4]), .q4(B_q7[3]), .q5(B_q7[2]), .q6(B_q7[1]),
    .q7(B_q7[0]));  // open: shift, in, clk, out, load, clr, d0, d1, d2, d3, d4, d5, d6, d7
  Shift_Register Q (
    .shift(or_1_out), .in(AC_out), .clk(clock_1_out), .out(Q_out), .q7(Q_q7));  // open: load, clr, d0, q0, d1, q1, d2, q2, d3, q3, d4, q4, d5, q5, d6, q6, d7
  assign not_2_out = ~B_q7;  // NOT_Gate not_2, 8 bits wide
  _1to8 u_1to8_1 (.INPUT(Q_q7), .OUTPUT(n1to8_1_output));
  Adder adder_1 (.a(in_1), .b(not_2_out), .out(adder_1_out));  // open: cin, cout
  or or_1 (or_1_out, not_3_out, counter_1_q);
  Shift_Register #(.length(1)) Q_n_1 (
    .shift(or_1_out), .in(Q_out), .clk(clock_1_out), .out(Q_n_1_out));  // open: load, clr, d0, q0
  xor xor_1 (xor_1_out, Q_n_1_out, Q_q7);
  _1to8 u_1to8_2 (.INPUT(Q_n_1_out), .OUTPUT(n1to8_2_output));
  assign and_2_out = adder_1_out & n1to8_3_output & n1to8_1_output;  // AND_Gate and_2, 8 bits wide
  assign and_3_out = B_q7 & n1to8_3_output & n1to8_2_output;  // AND_Gate and_3, 8 bits wide
  not not_3 (not_3_out, xor_1_out);
  _1to8 u_1to8_3 (.INPUT(xor_1_out), .OUTPUT(n1to8_3_output));
  assign or_2_out = and_2_out | and_3_out;  // OR_Gate or_2, 8 bits wide
  Counter #(.width(1), .max('h1)) counter_1 (
    .D(xor_1_out), .Q(counter_1_q), .clk(clock_1_out), .clr(not_3_out));  // open: load, count, carry
  Adder adder_2 (.a(or_2_out), .b(AC_q7), .out(adder_2_out));  // open: cin, cout
endmodule

module _1to8 (
  input  INPUT,
  output [7:0] OUTPUT
);


  assign OUTPUT = {8{INPUT}};
endmodule
