// Logisim project no-use.circ as structural Verilog: 1 circuit, main circuit main
module main (
  input  [1:0] in_1,
  input  [1:0] in_2
);

  wire and_1_out, clock_1_out, counter_1_carry, decoder_1_out0, decoder_1_out1, decoder_1_out2,
       decoder_1_out3, multiplexer_1_out, not_1_out, shift_register_1_out, shift_register_2_out,
       shift_register_3_out, shift_register_4_out;

  Counter #(.width(3), .max('h4), .ongoal("stay")) counter_1 (
    .carry(counter_1_carry), .clk(clock_1_out));  // open: load, D, count, Q, clr
  not not_1 (not_1_out, counter_1_carry);
  Clock clock_1 (.out(clock_1_out));
  Decoder #(.select(2), .enable("false")) decoder_1 (
    .out0(decoder_1_out0), .out1(decoder_1_out1), .out2(decoder_1_out2), .out3(decoder_1_out3), .sel(in_1));
  and and_1 (and_1_out, not_1_out, clock_1_out);
  Shift_Register #(.length(4)) shift_register_1 (
    .shift(decoder_1_out0), .in(multiplexer_1_out), .clk(and_1_out), .out(shift_register_1_out));  // open: load, clr, d0, q0, d1, q1, d2, q2, d3, q3
  Shift_Register #(.length(4)) shift_register_2 (
    .shift(decoder_1_out1), .in(multiplexer_1_out), .clk(and_1_out), .out(shift_register_2_out));  // open: load, clr, d0, q0, d1, q1, d2, q2, d3, q3
  Shift_Register #(.length(4)) shift_register_3 (
    .shift(decoder_1_out2), .in(multiplexer_1_out), .clk(and_1_out), .out(shift_register_3_out));  // open: load, clr, d0, q0, d1, q1, d2, q2, d3, q3
  Shift_Register #(.length(4)) shift_register_4 (
    .shift(decoder_1_out3), .in(multiplexer_1_out), .clk(and_1_out), .out(shift_register_4_out));  // open: load, clr, d0, q0, d1, q1, d2, q2, d3, q3
  Multiplexer #(.select(2), .enable("false")) multiplexer_1 (
    .in0(shift_register_1_out), .in1(shift_register_2_out), .in2(shift_register_3_out),
    .in3(shift_register_4_out), .out(multiplexer_1_out), .sel(in_2));
  Decoder #(.select(2), .enable("false")) decoder_2 (
    .out0(decoder_1_out0), .out1(decoder_1_out1), .out2(decoder_1_out2), .out3(decoder_1_out3), .sel(in_2));
endmodule
