// Logisim project ownDef3.circ as structural Verilog: 1 circuit, main circuit main
module main (
  input  [3:0] B,
  input  [3:0] A,
  input  [3:0] in_3,
  input  [1:0] in_4,
  input  s0,
  input  s1,
  input  s2,
  output [3:0] out_8
);

  wire and_2_out, and_3_out, and_5_out, not_2_out, not_3_out, not_4_out, or_1_out, xor_2_out;
  wire [1:0] or_2_out;
  wire [3:0] adder_1_out, and_1_out, multiplexer_1_out, multiplexer_2_out, not_1_out, shifter_1_out,
       shifter_2_out, xor_1_out;

  assign not_1_out = ~B;  // NOT_Gate not_1, 4 bits wide
  assign xor_1_out = A ^ B;  // XOR_Gate xor_1, 4 bits wide
  assign and_1_out = A & B;  // AND_Gate and_1, 4 bits wide
  Multiplexer #(.select(2), .width(4), .enable("false")) multiplexer_1 (
    .in0(B), .in1(not_1_out), .in2(not_1_out), .in3(in_3), .out(multiplexer_1_out), .sel({s0, s2}));
  not not_2 (not_2_out, s1);
  not not_3 (not_3_out, s2);
  Adder #(.width(4)) adder_1 (.a(A), .b(multiplexer_1_out), .out(adder_1_out), .cin(s0));  // open: cout
  Shifter #(.width(4), .shift("lr")) shifter_1 (.in(A), .\dist (in_4), .out(shifter_1_out));
  Shifter #(.width(4), .shift("rl")) shifter_2 (.in(A), .\dist (in_4), .out(shifter_2_out));
  Multiplexer #(.width(4), .enable("false")) multiplexer_2 (
    .in0(xor_1_out), .in1(and_1_out), .out(multiplexer_2_out), .sel(s2));
  not not_4 (not_4_out, s0);
  and and_2 (and_2_out, not_2_out, not_3_out);
  or or_1 (or_1_out, s0, s2);
  Multiplexer #(.select(2), .width(4), .enable("false")) multiplexer_3 (
    .in0(adder_1_out), .in1(shifter_1_out), .in2(shifter_2_out), .in3(multiplexer_2_out), .out(out_8),
    .sel(or_2_out));
  and and_3 (and_3_out, s0, and_2_out);
  xor xor_2 (xor_2_out, s1, s2);
  and and_4 (or_2_out[1], not_2_out, or_1_out);
  and and_5 (and_5_out, not_4_out, xor_2_out);
  or or_2 (or_2_out[0], and_5_out, and_3_out);
endmodule
