// Logisim project prac3.circ as structural Verilog: 1 circuit, main circuit main
module main (
  input  in_1,
  input  [2:0] in_2,
  input  in_3
);

  wire adder_1_out, and_1_out, and_2_out, clock_1_out, counter_1_carry, multiplexer_1_out, not_1_out,
       not_2_out, or_1_out, shift_register_1_out, shift_register_2_out, shifter_1_out, shifter_2_out,
       subtractor_1_out, xor_1_out;

  Counter #(.width(3), .max('h4), .ongoal("stay")) counter_1 (
    .carry(counter_1_carry), .clk(clock_1_out));  // open: load, D, count, Q, clr
  Clock clock_1 (.out(clock_1_out));
  not not_1 (not_1_out, counter_1_carry);
  and and_1 (and_1_out, not_1_out, clock_1_out);
  Shift_Register #(.length(4)) shift_register_1 (
    .shift(in_1), .in(shift_register_1_out), .clk(and_1_out), .out(shift_register_1_out));  // open: load, clr, d0, q0, d1, q1, d2, q2, d3, q3
  Shift_Register #(.length(4)) shift_register_2 (
    .shift(in_1), .in(shift_register_2_out), .clk(and_1_out), .out(shift_register_2_out));  // open: load, clr, d0, q0, d1, q1, d2, q2, d3, q3
  not not_2 (not_2_out, shift_register_1_out);
  and and_2 (and_2_out, shift_register_1_out, shift_register_2_out);
  or or_1 (or_1_out, shift_register_1_out, shift_register_2_out);
  xor xor_1 (xor_1_out, shift_register_1_out, shift_register_2_out);
  Adder #(.width(1)) adder_1 (
    .a(shift_register_1_out), .b(shift_register_2_out), .out(adder_1_out));  // open: cin, cout
  Subtractor #(.width(1)) subtractor_1 (
    .a(shift_register_1_out), .b(shift_register_2_out), .out(subtractor_1_out));  // open: bin, bout
  Shifter #(.width(1), .shift("lr")) shifter_1 (.in(shift_register_1_out), .\dist (in_3), .out(shifter_1_out));
  Shifter #(.width(1)) shifter_2 (.in(shift_register_1_out), .\dist (in_3), .out(shifter_2_out));
  Multiplexer #(.select(3), .enable("false")) multiplexer_1 (
    .in0(and_2_out), .in1(or_1_out), .in2(not_2_out), .in3(xor_1_out), .in4(adder_1_out),
    .in5(subtractor_1_out), .in6(shifter_1_out), .in7(shifter_2_out), .out(multiplexer_1_out), .sel(in_2));
  Shift_Register #(.length(4)) shift_register_3 (
    .shift(in_1), .in(multiplexer_1_out), .clk(and_1_out));  // open: out, load, clr, d0, q0, d1, q1, d2, q2, d3, q3
endmodule
