// Logisim project prac3ct.circ as structural Verilog: 4 circuits, main circuit main
module main (
);

  wire and_1_out, and_2_out, and_3_out, and_4_out, and_5_out, and_6_out, and_7_out, b_b8, b_b11, b_out_7,
       b_out_8, b_out_11, clock_1_out, decoder_1_out0, decoder_1_out1, decoder_1_out2, decoder_1_out3,
       decoder_1_out4, decoder_1_out5, decoder_1_out6, decoder_1_out7, decoder_2_out0, decoder_2_out1,
       decoder_2_out2, decoder_2_out3, decoder_2_out4, decoder_2_out5, decoder_2_out6, decoder_2_out7,
       or_1_out, r_out;
  wire [2:0] decode_1_out_2, SC_q;
  wire [15:0] AC_q, adder_1_out, and_8_out, and_9_out, and_10_out, and_11_out, and_12_out, and_13_out, DR_q,
       IR_q, n1to16_1_out_2, n1to16_2_out_2, n1to16_3_out_2, n1to16_4_out_2, n1to16_5_out_2, n1to16_6_out_2,
       not_1_out, or_2_out;

  Clock clock_1 (.out(clock_1_out));
  Counter #(.width(3), .max('h7)) SC (.Q(SC_q), .clk(clock_1_out));  // open: load, D, count, carry, clr
  Decoder #(.select(3), .enable("false")) decoder_1 (
    .out0(decoder_1_out0), .out1(decoder_1_out1), .out2(decoder_1_out2), .out3(decoder_1_out3),
    .out4(decoder_1_out4), .out5(decoder_1_out5), .out6(decoder_1_out6), .out7(decoder_1_out7), .sel(SC_q));
  Register #(.width(16)) IR (.Q(IR_q), .clk(clock_1_out));  // open: D, en, clr
  Register #(.width(16)) AC (.D(or_2_out), .en(or_1_out), .Q(AC_q), .clk(clock_1_out), .clr(and_1_out));
  Register #(.width(16)) DR (.Q(DR_q), .clk(clock_1_out));  // open: D, en, clr
  and and_1 (and_1_out, b_b11, r_out);
  decode decode_1 (.in_1(IR_q), .out_2(decode_1_out_2));
  _16to12 b (
    .in_1(IR_q), .out_7(b_out_7), .out_8(b_out_8), .b8(b_b8), .out_11(b_out_11), .b11(b_b11));  // open: b0, out_3, out_4, out_5, out_6, b9, out_12
  Decoder #(.select(3), .enable("false")) decoder_2 (
    .out0(decoder_2_out0), .out1(decoder_2_out1), .out2(decoder_2_out2), .out3(decoder_2_out3),
    .out4(decoder_2_out4), .out5(decoder_2_out5), .out6(decoder_2_out6), .out7(decoder_2_out7),
    .sel(decode_1_out_2));
  // AND_Gate incac has open pins: in0=b_out_7, in1=r_out, out=open
  and and_2 (and_2_out, b_out_8, r_out);
  and and_3 (and_3_out, b_b8, r_out);
  and and_4 (and_4_out, b_out_11, r_out);
  and r (r_out, decoder_2_out7, decoder_1_out3);
  and and_5 (and_5_out, decoder_1_out5, decoder_2_out0);
  and and_6 (and_6_out, decoder_2_out1, decoder_1_out5);
  and and_7 (and_7_out, decoder_2_out2, decoder_1_out5);
  or or_1 (or_1_out, and_5_out, and_6_out, and_7_out, and_2_out, and_3_out, and_4_out);
  _1to16 u_1to16_1 (.in_1(and_2_out), .out_2(n1to16_1_out_2));
  _1to16 u_1to16_2 (.in_1(and_3_out), .out_2(n1to16_2_out_2));
  _1to16 u_1to16_3 (.in_1(and_4_out), .out_2(n1to16_3_out_2));
  _1to16 u_1to16_4 (.in_1(and_5_out), .out_2(n1to16_4_out_2));
  _1to16 u_1to16_5 (.in_1(and_6_out), .out_2(n1to16_5_out_2));
  _1to16 u_1to16_6 (.in_1(and_7_out), .out_2(n1to16_6_out_2));
  assign not_1_out = ~AC_q;  // NOT_Gate not_1, 16 bits wide
  Adder #(.width(16)) adder_1 (.a(AC_q), .b(DR_q), .out(adder_1_out));  // open: cin, cout
  assign and_8_out = n1to16_4_out_2 & AC_q & DR_q;  // AND_Gate and_8, 16 bits wide
  assign and_9_out = n1to16_5_out_2 & adder_1_out;  // AND_Gate and_9, 16 bits wide
  assign and_10_out = n1to16_6_out_2 & DR_q;  // AND_Gate and_10, 16 bits wide
  assign and_11_out = n1to16_1_out_2 & not_1_out;  // AND_Gate and_11, 16 bits wide
  assign and_12_out = n1to16_2_out_2 & AC_q;  // AND_Gate and_12, 16 bits wide
  assign and_13_out = n1to16_3_out_2 & AC_q;  // AND_Gate and_13, 16 bits wide
  assign or_2_out = and_8_out | and_9_out | and_10_out | and_11_out | and_12_out | and_13_out;  // OR_Gate or_2, 16 bits wide

  // Notes on the sheet:
  //   timing signal
  //   decoding operation
endmodule

module _16to12 (
  input  [15:0] in_1,
  output b0,
  output out_3,
  output out_4,
  output out_5,
  output out_6,
  output out_7,
  output out_8,
  output b8,
  output b9,
  output out_11,
  output out_12,
  output b11
);


  assign b0 = in_1[0];
  assign b8 = in_1[7];
  assign b9 = in_1[8];
  assign b11 = in_1[11];
  assign out_3 = in_1[1];
  assign out_4 = in_1[2];
  assign out_5 = in_1[3];
  assign out_6 = in_1[4];
  assign out_7 = in_1[5];
  assign out_8 = in_1[6];
  assign out_11 = in_1[9];
  assign out_12 = in_1[10];
endmodule

module decode (
  input  [15:0] in_1,
  output [2:0] out_2
);


  assign out_2 = in_1[14:12];
endmodule

module _1to16 (
  input  in_1,
  output [15:0] out_2
);


  assign out_2 = {16{in_1}};
endmodule
