// Logisim project read.circ as structural Verilog: 2 circuits, main circuit main
module main (
  input  [7:0] Data,
  input  [7:0] Mask,
  output [7:0] out_3
);

  wire check_1_out_4, check_2_out_4, check_3_out_4, check_4_out_4, clock_1_out, not_1_out,
       shift_register_1_q0, shift_register_1_q1, shift_register_1_q2, shift_register_1_q3;
  wire [1:0] priority_encoder_1_out;
  wire [7:0] register_1_q, register_2_q, register_3_q, register_4_q;

  Register register_1 (.Q(register_1_q));  // open: D, en, clk, clr
  Register register_2 (.Q(register_2_q));  // open: D, en, clk, clr
  Register register_3 (.Q(register_3_q));  // open: D, en, clk, clr
  Register register_4 (.Q(register_4_q));  // open: D, en, clk, clr
  check check_1 (.Reg(register_1_q), .Mask(Mask), .Data(Data), .out_4(check_1_out_4));
  check check_2 (.Reg(register_2_q), .Mask(Mask), .Data(Data), .out_4(check_2_out_4));
  check check_3 (.Reg(register_3_q), .Mask(Mask), .Data(Data), .out_4(check_3_out_4));
  check check_4 (.Reg(register_4_q), .Mask(Mask), .Data(Data), .out_4(check_4_out_4));
  Clock clock_1 (.out(clock_1_out));
  not not_1 (not_1_out, 1'b1);
  Shift_Register #(.length(4)) shift_register_1 (
    .shift(not_1_out), .clk(clock_1_out), .load(1'b1), .d0(check_1_out_4), .q0(shift_register_1_q0),
    .d1(check_2_out_4), .q1(shift_register_1_q1), .d2(check_3_out_4), .q2(shift_register_1_q2),
    .d3(check_4_out_4), .q3(shift_register_1_q3));  // open: in, out, clr
  Multiplexer #(.select(2), .width(8), .enable("false")) multiplexer_1 (
    .in0(register_1_q), .in1(register_2_q), .in2(register_3_q), .in3(register_4_q), .out(out_3),
    .sel(priority_encoder_1_out));
  Priority_Encoder #(.select(2)) priority_encoder_1 (
    .in0(shift_register_1_q0), .in1(shift_register_1_q1), .in2(shift_register_1_q2),
    .in3(shift_register_1_q3), .out(priority_encoder_1_out));  // open: gs, en_out, en_in
endmodule

module check (
  input  [7:0] Reg,
  input  [7:0] Mask,
  input  [7:0] Data,
  output out_4
);

  wire [7:0] and_1_out, and_2_out, xnor_1_out;

  assign and_1_out = Reg & Mask;  // AND_Gate and_1, 8 bits wide
  assign and_2_out = Mask & Data;  // AND_Gate and_2, 8 bits wide
  assign xnor_1_out = ~(and_1_out ^ and_2_out);  // XNOR_Gate xnor_1, 8 bits wide
  and and_3 (out_4, xnor_1_out[0], xnor_1_out[1], xnor_1_out[2], xnor_1_out[3], xnor_1_out[4], xnor_1_out[5], xnor_1_out[6], xnor_1_out[7]);
endmodule
