// Logisim project signed_multiplication.circ as structural Verilog: 1 circuit, main circuit main
module main (
);

  wire clock_1_out, counter_1_carry, not_1_out;
  wire [3:0] A_q, adder_1_out, B_q, Q_q, shifter_1_out, shifter_1_out_2;
  wire [8:0] multiplexer_1_out;
  wire [8:8] adder_1_cout, e_q, shifter_1_out_3;

  Clock clock_1 (.out(clock_1_out));
  Counter #(.width(4), .max('h4), .ongoal("stay")) counter_1 (
    .carry(counter_1_carry), .clk(clock_1_out));  // open: load, D, count, Q, clr
  not not_1 (not_1_out, counter_1_carry);
  Register #(.width(1)) e (.D(shifter_1_out_3[8]), .en(not_1_out), .Q(e_q[8]), .clk(clock_1_out));  // open: clr
  Register #(.width(4)) A (.D(shifter_1_out_2), .en(not_1_out), .Q(A_q), .clk(clock_1_out));  // open: clr
  Register #(.width(4)) B (.en(not_1_out), .Q(B_q), .clk(clock_1_out));  // open: D, clr
  Register #(.width(4)) Q (.D(shifter_1_out), .en(not_1_out), .Q(Q_q), .clk(clock_1_out));  // open: clr
  Adder #(.width(4)) adder_1 (.a(A_q), .b(B_q), .out(adder_1_out), .cout(adder_1_cout[8]));  // open: cin
  Multiplexer #(.width(9)) multiplexer_1 (
    .in0({e_q[8], A_q, Q_q}), .in1({adder_1_cout[8], adder_1_out, Q_q}), .out(multiplexer_1_out), .sel(Q_q[0]));  // open: en
  Shifter #(.width(9), .shift("lr")) shifter_1 (
    .in(multiplexer_1_out), .\dist (4'b0001), .out({shifter_1_out_3[8], shifter_1_out_2, shifter_1_out}));
endmodule
