// Logisim project stack.circ as structural Verilog: 1 circuit, main circuit main
// 0x7
module main (
  input  _0___POP,
  input  [15:0] Input,
  input  [3:0] in_3,
  input  [3:0] in_4,
  output [15:0] Output,
  output [3:0] out_6
);

  wire and_1_out, and_2_out, button_1_out, comparator_1_eq, comparator_1_lt, comparator_2_lt, not_1_out;

  Button button_1 (.out(button_1_out));
  not not_1 (not_1_out, _0___POP);
  Counter #(.width(4), .max('hf)) counter_1 (
    .load(not_1_out), .count(1'b1), .Q(out_6), .clk(button_1_out));  // open: D, carry, clr
  Comparator #(.width(4)) comparator_1 (.a(out_6), .b(in_3), .eq(comparator_1_eq), .lt(comparator_1_lt));  // open: gt
  Comparator #(.width(4)) comparator_2 (.a(out_6), .b(in_4), .lt(comparator_2_lt));  // open: gt, eq
  and and_1 (and_1_out, _0___POP, comparator_1_lt);
  and and_2 (and_2_out, not_1_out, comparator_1_lt);
  RAM #(.addrWidth(4), .dataWidth(16), .bus("separate")) ram_1 (
    .addr(out_6), .din(Input), .data(Output), .str(and_1_out), .clk(button_1_out), .ld(and_2_out));  // open: sel, clr
  LED led_1 (.in(comparator_1_eq));
  LED led_2 (.in(comparator_2_lt));

  // Notes on the sheet:
  //   Length Of Stack
  //   Lower Bound Of Stack
  //   Selection for Action
  //   1: PUSH
  //   Over Flow
  //   Under FLow
endmodule
